// Logisim project smips.circ as structural Verilog: 9 circuits, main circuit Board
module Board (
);

  wire CLK, HALT, MEM_WE, RESET, TTY_WE;
  wire [3:0] MEM_BE;
  wire [6:0] TTY_DATA;
  wire [31:0] MEM_ADDR, MEM_RDATA, MEM_WDATA;

  Clock Reloj (.out(CLK));
  Button u_Reset (.out(RESET));
  CPU cpu_1 (
    .CLK(CLK), .RESET(RESET), .MEM_RDATA(MEM_RDATA), .MEM_ADDR(MEM_ADDR), .MEM_WDATA(MEM_WDATA),
    .MEM_BE(MEM_BE), .MEM_WE(MEM_WE), .TTY_DATA(TTY_DATA), .TTY_WE(TTY_WE), .HALT(HALT));
  TTY #(.cols(48), .rows(12)) tty_1 (.data(TTY_DATA), .clk(CLK), .we(TTY_WE), .clr(RESET));
  Memory memory_1 (.CLK(CLK), .ADDR(MEM_ADDR), .WDATA(MEM_WDATA), .BE(MEM_BE), .WE(MEM_WE), .RDATA(MEM_RDATA));
  LED u_Halt (.in(HALT));

  // Notes on the sheet:
  //   S-MIPS | Board
  //   No modificar: la CPU se implementa dentro del subcircuito CPU.
endmodule

module CPU (
  input  CLK,
  input  RESET,
  input  [31:0] MEM_RDATA,
  output [31:0] MEM_ADDR,
  output [31:0] MEM_WDATA,
  output [3:0] MEM_BE,
  output MEM_WE,
  output [6:0] TTY_DATA,
  output TTY_WE,
  output HALT
);


  // Notes on the sheet:
  //   CPU S-MIPS: implementar aqui
  //   No cambiar nombres, anchos ni sentido de los pines: la placa depende de ellos.
endmodule

module Memory (
  input  CLK,
  input  [31:0] ADDR,
  input  [31:0] WDATA,
  input  [3:0] BE,
  input  WE,
  output [31:0] RDATA
);

  RAM #(.addrWidth(12), .asyncread("true"), .byteenables("byteEnables"), .dataWidth(32), .\type ("nonvolatile")) Main_Memory (
    .addr(ADDR[13:2]), .we(WE), .oe(1'b1), .clk(CLK), .din(WDATA), .dout(RDATA), .be3(BE[3]), .be2(BE[2]),
    .be1(BE[1]), .be0(BE[0]));

  // Other names for the same wires on the sheet: A[11:0] = ADDR[13:2]

  // Notes on the sheet:
  //   Memoria unificada: 4096 palabras de 32 bits (16 KiB), little-endian
  //   Lectura combinacional; escritura en el flanco de subida de CLK con WE=1, solo en los bytes con BE=1.
  //   Se usan los bits 13..2 de ADDR; los demas se ignoran (el espacio se repite cada 16 KiB).
endmodule

module ALU (
  input  [31:0] A,
  input  [31:0] B,
  input  [2:0] ALUControl,
  input  [4:0] Shamt,
  output [31:0] Result,
  output Zero
);

  wire comparator_1_lt;
  wire [31:0] adder_1_out, and_1_out, bit_extender_1_out, or_1_out, shifter_1_out, shifter_2_out,
       shifter_3_out, subtractor_1_out;

  Adder #(.width(32)) adder_1 (.a(A), .b(B), .out(adder_1_out));  // open: cin, cout
  Subtractor #(.width(32)) subtractor_1 (.a(A), .b(B), .out(subtractor_1_out));  // open: bin, bout
  Comparator #(.width(32)) comparator_1 (.a(A), .b(B), .lt(comparator_1_lt));  // open: gt, eq
  Shifter #(.width(32)) shifter_1 (.in(B), .\dist (Shamt), .out(shifter_1_out));
  Shifter #(.shift("lr"), .width(32)) shifter_2 (.in(B), .\dist (Shamt), .out(shifter_2_out));
  Shifter #(.width(32)) shifter_3 (.in(B), .\dist (5'b10000), .out(shifter_3_out));
  assign and_1_out = A & B;  // AND_Gate and_1, 32 bits wide
  assign or_1_out = A | B;  // OR_Gate or_1, 32 bits wide
  assign bit_extender_1_out = {{31{1'b0}}, comparator_1_lt};  // Bit_Extender bit_extender_1
  Multiplexer #(.select(3), .width(32)) multiplexer_1 (
    .in0(adder_1_out), .in1(subtractor_1_out), .in2(and_1_out), .in3(or_1_out), .in4(bit_extender_1_out),
    .in5(shifter_1_out), .in6(shifter_2_out), .in7(shifter_3_out), .out(Result), .sel(ALUControl));
  Comparator #(.width(32)) comparator_2 (.a(Result), .b({32{1'b0}}), .eq(Zero));  // open: gt, lt

  // Other names for the same wires on the sheet: ALU[2:0] = ALUControl
endmodule

module Register_File (
  input  [4:0] ReadReg2,
  input  [4:0] WriteReg,
  input  [31:0] WriteData,
  input  RegWrite,
  input  RESET,
  input  [4:0] ReadReg1,
  output [31:0] ReadData1,
  output [31:0] ReadData2
);

  wire clock_1_out, decoder_1_out1, decoder_1_out2, decoder_1_out3, decoder_1_out4, decoder_1_out5,
       decoder_1_out6, decoder_1_out7, decoder_1_out8, decoder_1_out9, decoder_1_out10, decoder_1_out11,
       decoder_1_out12, decoder_1_out13, decoder_1_out14, decoder_1_out15, decoder_1_out16, decoder_1_out17,
       decoder_1_out18, decoder_1_out19, decoder_1_out20, decoder_1_out21, decoder_1_out22, decoder_1_out23,
       decoder_1_out24, decoder_1_out25, decoder_1_out26, decoder_1_out27, decoder_1_out28, decoder_1_out29,
       decoder_1_out30, decoder_1_out31, or_1_out, or_2_out;
  wire [31:0] multiplexer_1_out, multiplexer_2_out, register_1_q, register_2_q, register_3_q, register_4_q,
       register_5_q, register_6_q, register_7_q, register_8_q, register_9_q, register_10_q, register_11_q,
       register_12_q, register_13_q, register_14_q, register_15_q, register_16_q, register_17_q,
       register_18_q, register_19_q, register_20_q, register_21_q, register_22_q, register_23_q,
       register_24_q, register_25_q, register_26_q, register_27_q, register_28_q, register_29_q,
       register_30_q, register_31_q, register_32_q, undriven;

  Clock clock_1 (.out(clock_1_out));
  Decoder #(.select(5)) decoder_1 (
    .out1(decoder_1_out1), .out2(decoder_1_out2), .out3(decoder_1_out3), .out4(decoder_1_out4),
    .out5(decoder_1_out5), .out6(decoder_1_out6), .out7(decoder_1_out7), .out8(decoder_1_out8),
    .out9(decoder_1_out9), .out10(decoder_1_out10), .out11(decoder_1_out11), .out12(decoder_1_out12),
    .out13(decoder_1_out13), .out14(decoder_1_out14), .out15(decoder_1_out15), .out16(decoder_1_out16),
    .out17(decoder_1_out17), .out18(decoder_1_out18), .out19(decoder_1_out19), .out20(decoder_1_out20),
    .out21(decoder_1_out21), .out22(decoder_1_out22), .out23(decoder_1_out23), .out24(decoder_1_out24),
    .out25(decoder_1_out25), .out26(decoder_1_out26), .out27(decoder_1_out27), .out28(decoder_1_out28),
    .out29(decoder_1_out29), .out30(decoder_1_out30), .out31(decoder_1_out31), .sel(WriteReg), .en(RegWrite));  // open: out0
  or or_1 (or_1_out, decoder_1_out28, RESET);
  or or_2 (or_2_out, decoder_1_out29, RESET);
  Register #(.width(32)) register_1 (.D(WriteData), .clk(clock_1_out), .Q(register_1_q));  // open: en, clr
  Register #(.width(32)) register_2 (
    .D(WriteData), .en(decoder_1_out1), .clk(clock_1_out), .Q(register_2_q), .clr(RESET));
  Register #(.width(32)) register_3 (
    .D(WriteData), .en(decoder_1_out2), .clk(clock_1_out), .Q(register_3_q), .clr(RESET));
  Register #(.width(32)) register_4 (
    .D(WriteData), .en(decoder_1_out3), .clk(clock_1_out), .Q(register_4_q), .clr(RESET));
  Register #(.width(32)) register_5 (
    .D(WriteData), .en(decoder_1_out4), .clk(clock_1_out), .Q(register_5_q), .clr(RESET));
  Register #(.width(32)) register_6 (
    .D(WriteData), .en(decoder_1_out5), .clk(clock_1_out), .Q(register_6_q), .clr(RESET));
  Register #(.width(32)) register_7 (
    .D(WriteData), .en(decoder_1_out6), .clk(clock_1_out), .Q(register_7_q), .clr(RESET));
  Register #(.width(32)) register_8 (
    .D(WriteData), .en(decoder_1_out7), .clk(clock_1_out), .Q(register_8_q), .clr(RESET));
  Register #(.width(32)) register_9 (
    .D(WriteData), .en(decoder_1_out8), .clk(clock_1_out), .Q(register_9_q), .clr(RESET));
  Register #(.width(32)) register_10 (
    .D(WriteData), .en(decoder_1_out9), .clk(clock_1_out), .Q(register_10_q), .clr(RESET));
  Register #(.width(32)) register_11 (
    .D(WriteData), .en(decoder_1_out10), .clk(clock_1_out), .Q(register_11_q), .clr(RESET));
  Register #(.width(32)) register_12 (
    .D(WriteData), .en(decoder_1_out11), .clk(clock_1_out), .Q(register_12_q), .clr(RESET));
  Register #(.width(32)) register_13 (
    .D(WriteData), .en(decoder_1_out12), .clk(clock_1_out), .Q(register_13_q), .clr(RESET));
  Register #(.width(32)) register_14 (
    .D(WriteData), .en(decoder_1_out13), .clk(clock_1_out), .Q(register_14_q), .clr(RESET));
  Register #(.width(32)) register_15 (
    .D(WriteData), .en(decoder_1_out14), .clk(clock_1_out), .Q(register_15_q), .clr(RESET));
  Register #(.width(32)) register_16 (
    .D(WriteData), .en(decoder_1_out15), .clk(clock_1_out), .Q(register_16_q), .clr(RESET));
  Register #(.width(32)) register_17 (
    .D(WriteData), .en(decoder_1_out16), .clk(clock_1_out), .Q(register_17_q), .clr(RESET));
  Register #(.width(32)) register_18 (
    .D(WriteData), .en(decoder_1_out17), .clk(clock_1_out), .Q(register_18_q), .clr(RESET));
  Register #(.width(32)) register_19 (
    .D(WriteData), .en(decoder_1_out18), .clk(clock_1_out), .Q(register_19_q), .clr(RESET));
  Register #(.width(32)) register_20 (
    .D(WriteData), .en(decoder_1_out19), .clk(clock_1_out), .Q(register_20_q), .clr(RESET));
  Register #(.width(32)) register_21 (
    .D(WriteData), .en(decoder_1_out20), .clk(clock_1_out), .Q(register_21_q), .clr(RESET));
  Register #(.width(32)) register_22 (
    .D(WriteData), .en(decoder_1_out21), .clk(clock_1_out), .Q(register_22_q), .clr(RESET));
  Register #(.width(32)) register_23 (
    .D(WriteData), .en(decoder_1_out22), .clk(clock_1_out), .Q(register_23_q), .clr(RESET));
  Register #(.width(32)) register_24 (
    .D(WriteData), .en(decoder_1_out23), .clk(clock_1_out), .Q(register_24_q), .clr(RESET));
  Register #(.width(32)) register_25 (
    .D(WriteData), .en(decoder_1_out24), .clk(clock_1_out), .Q(register_25_q), .clr(RESET));
  Register #(.width(32)) register_26 (
    .D(WriteData), .en(decoder_1_out25), .clk(clock_1_out), .Q(register_26_q), .clr(RESET));
  Register #(.width(32)) register_27 (
    .D(WriteData), .en(decoder_1_out26), .clk(clock_1_out), .Q(register_27_q), .clr(RESET));
  Register #(.width(32)) register_28 (
    .D(WriteData), .en(decoder_1_out27), .clk(clock_1_out), .Q(register_28_q), .clr(RESET));
  Register #(.width(32)) register_29 (
    .D(multiplexer_1_out), .en(or_1_out), .clk(clock_1_out), .Q(register_29_q));  // open: clr
  Multiplexer #(.width(32)) multiplexer_1 (.in0(WriteData), .in1(undriven), .out(multiplexer_1_out), .sel(RESET));
  Register #(.width(32)) register_30 (
    .D(multiplexer_2_out), .en(or_2_out), .clk(clock_1_out), .Q(register_30_q));  // open: clr
  Multiplexer #(.width(32)) multiplexer_2 (.in0(WriteData), .in1(32'h3ffc), .out(multiplexer_2_out));  // open: sel
  Register #(.width(32)) register_31 (
    .D(WriteData), .en(decoder_1_out30), .clk(clock_1_out), .Q(register_31_q), .clr(RESET));
  Register #(.width(32)) register_32 (
    .D(WriteData), .en(decoder_1_out31), .clk(clock_1_out), .Q(register_32_q), .clr(RESET));
  Multiplexer #(.select(5), .width(32)) multiplexer_3 (
    .in0(register_1_q), .in1(register_2_q), .in2(register_3_q), .in3(register_4_q), .in4(register_5_q),
    .in5(register_6_q), .in6(register_7_q), .in7(register_8_q), .in8(register_9_q), .in9(register_10_q),
    .in10(register_11_q), .in11(register_12_q), .in12(register_13_q), .in13(register_14_q),
    .in14(register_15_q), .in15(register_16_q), .in16(register_17_q), .in17(register_18_q),
    .in18(register_19_q), .in19(register_20_q), .in20(register_21_q), .in21(register_22_q),
    .in22(register_23_q), .in23(register_24_q), .in24(register_25_q), .in25(register_26_q),
    .in26(register_27_q), .in27(register_28_q), .in28(register_29_q), .in29(register_30_q),
    .in30(register_31_q), .in31(register_32_q), .out(ReadData1), .sel(ReadReg1));
  Multiplexer #(.select(5), .width(32)) multiplexer_4 (
    .in0(register_1_q), .in1(register_2_q), .in2(register_3_q), .in3(register_4_q), .in4(register_5_q),
    .in5(register_6_q), .in6(register_7_q), .in7(register_8_q), .in8(register_9_q), .in9(register_10_q),
    .in10(register_11_q), .in11(register_12_q), .in12(register_13_q), .in13(register_14_q),
    .in14(register_15_q), .in15(register_16_q), .in16(register_17_q), .in17(register_18_q),
    .in18(register_19_q), .in19(register_20_q), .in20(register_21_q), .in21(register_22_q),
    .in22(register_23_q), .in23(register_24_q), .in24(register_25_q), .in25(register_26_q),
    .in26(register_27_q), .in27(register_28_q), .in28(register_29_q), .in29(register_30_q),
    .in30(register_31_q), .in31(register_32_q), .out(ReadData2), .sel(ReadReg2));

  // Other names for the same wires on the sheet: AB[4:0] = ReadReg1; AC[4:0] = ReadReg2; SelDec[4:0] = WriteReg

  // Notes on the sheet:
  //   Registro 29 → 0x00003FFC
  //   Registro $gp (Registro 28) → 0x00001800
  //   El resto de registros → 0x00000000
endmodule

module Datapath (
  input  CLK,
  input  RESET,
  input  [31:0] MEM_RDATA,
  input  PCWriteFinal,
  input  IRWrite,
  input  RegWrite,
  input  [1:0] RegDst,
  input  [1:0] MemToReg,
  input  ALUSrcA,
  input  ALUSrcB,
  input  [2:0] ALUOp,
  input  PCSource,
  input  IorD,
  input  IsByte,
  input  IsUnsigned,
  output [31:0] MEM_ADDR,
  output [31:0] MEM_WDATA,
  output [3:0] MEM_BE,
  output [5:0] OpCode,
  output [5:0] Funct,
  output Zero,
  output [31:0] V0_Val,
  output [6:0] A0_Val
);

  Register #(.width(32)) PC ();  // open: D, en, clk, Q, clr
  Register #(.trigger("falling"), .width(32)) IR ();  // open: D, en, clk, Q, clr
  Register #(.width(32)) MDR ();  // open: D, en, clk, Q, clr
  Register #(.width(32)) A ();  // open: D, en, clk, Q, clr
  Register #(.width(32)) B ();  // open: D, en, clk, Q, clr
  Register #(.width(32)) ALUOut ();  // open: D, en, clk, Q, clr
endmodule

module Instruction_Decoder (
  input  [5:0] Opcode,
  input  [5:0] Funct,
  output [2:0] ALUOp,
  output ImmType,
  output IsRType,
  output IsBranch,
  output IsBeq,
  output IsBne,
  output IsJump,
  output IsJal,
  output IsJr,
  output IsSyscall,
  output IsLoad,
  output IsStore,
  output IsByte,
  output IsUnsigned,
  output Legal,
  output Illegal
);

  wire add, addiu, addu, and1, C, j, jr, lb, lui, lw, or1, or_6_out, ori, sb, sll1, slt, slti, srl1, sub, sw,
       syscall;

  Decoder #(.select(6)) decoder_1 (
    .out0(IsRType), .out2(j), .out3(IsJal), .out4(IsBeq), .out5(IsBne), .out8(IsJr), .out9(addiu),
    .out10(slti), .out12(IsSyscall), .out13(ori), .out15(lui), .out32(lb), .out35(lw), .out36(IsUnsigned),
    .out40(sb), .out43(sw), .sel(Opcode));  // open: out1, out6, out7, out11, out14, out16, out17, out18, out19, out20, out21, out22, out23, out24, out25, out26, out27, out28, out29, out30, out31, out33, out34, out37, out38, out39, out41, out42, out44, out45, out46, out47, out48, out49, out50, out51, out52, out53, out54, out55, out56, out57, out58, out59, out60, out61, out62, out63, en
  Decoder #(.select(6)) decoder_2 (
    .out0(sll1), .out2(srl1), .out8(jr), .out12(syscall), .out32(add), .out33(addu), .out34(sub),
    .out36(and1), .out37(or1), .out42(slt), .sel(Funct), .en(C));  // open: out1, out3, out4, out5, out6, out7, out9, out10, out11, out13, out14, out15, out16, out17, out18, out19, out20, out21, out22, out23, out24, out25, out26, out27, out28, out29, out30, out31, out35, out38, out39, out40, out41, out43, out44, out45, out46, out47, out48, out49, out50, out51, out52, out53, out54, out55, out56, out57, out58, out59, out60, out61, out62, out63
  or or_1 (ALUOp[0], slt, slti, sll1, srl1, lui);
  or or_2 (ALUOp[1], and1, IsSyscall, or1, ori, srl1, lui);
  or or_3 (ALUOp[2], sub, IsBeq, IsBne, or1, ori, sll1, lui);
  or or_4 (Legal, j, IsJal, IsBeq, IsBne, IsJr, addiu, slti, IsSyscall, ori, lui, lb, lw, IsUnsigned, sb, sw, sll1, srl1, jr, syscall, add, addu, sub, and1, or1, slt);
  not not_1 (Illegal, Legal);
  or or_5 (IsLoad, lb, lw, IsUnsigned);
  or or_6 (or_6_out, IsSyscall, ori, lui);
  not not_2 (ImmType, or_6_out);
  or or_7 (IsBranch, IsBeq, IsBne);
  or or_8 (IsJump, j, IsJal);
  or or_9 (IsStore, sb, sw);
  or or_10 (IsByte, lb, IsUnsigned, sb);

  // Other names for the same wires on the sheet: addi = IsJr; andi = IsSyscall; beq = IsBeq; bne = IsBne; jal = IsJal;
  //   lbu = IsUnsigned; RType = IsRType

  // Notes on the sheet:
  //   Decoder_Opcode
  //   Decoder_Funct
  //   Bit2
  //   Bit1
  //   Bit0
  //   ALUOp | 3 bits (Código de la ALU: 000=ADD, 001=SUB, 010=AND, etc.)
  //   ImmType | 1 bit (0 = Zero-extension para andi/ori, 1 = Sign-extension para addi/lw/sw/beq/bne)
  //   IsRType | 1 bit (1 si Opcode == 0x00)
  //   IsBranch | 1 bit (1 si es beq u bne)
  //   IsBeq | 1 bit (1 si es beq)
  //   IsBne | 1 bit (1 si es bne)
  //   IsJump | 1 bit (1 si es j o jal)
  //   IsJal | 1 bit (1 si es jal)
  //   IsJr | 1 bit (1 si Opcode == 0x00 y Funct == 0x08)
  //   IsSyscall | 1 bit (1 si Opcode == 0x00 y Funct == 0x0C)
  //   IsLoad | 1 bit (1 si es lw, lb, o lbu)
  //   IsStore | 1 bit (1 si es sw o sb)
  //   IsByte | 1 bit (1 si es lb, lbu o sb)
  //   IsUnsigned | 1 bit (1 si es lbu)
  //   Illegal | 1 bit (1 si la instrucción no pertenece a la lista S-MIPS)
endmodule

module Control_Unit (
  input  CLK,
  input  RESET,
  input  IsRType,
  input  IsLoad,
  input  IsStore,
  input  IsBranch,
  input  IsJump,
  input  IsJal,
  input  IsJr,
  input  IsSyscall,
  input  Illegal,
  input  [31:0] V0_Val,
  output PCWrite,
  output PCWriteCond,
  output IorD,
  output IRWrite,
  output RegWrite,
  output [1:0] RegDst,
  output [1:0] MemToReg,
  output ALUSrcA,
  output [1:0] ALUSrcB,
  output MEM_WE,
  output TTY_WE,
  output HALT,
  output [1:0] PCSource
);

  wire and_1_out, decoder_1_out1, decoder_1_out2, decoder_1_out3, decoder_1_out4, decoder_1_out5,
       decoder_1_out8, decoder_1_out11, decoder_1_out12, decoder_1_out13, or_1_out, V0;
  wire [3:0] CurrentState, IsLoadMux, multiplexer_1_out, multiplexer_2_out, multiplexer_4_out,
       multiplexer_5_out, multiplexer_6_out, multiplexer_8_out, multiplexer_9_out, S_ID, V0Mux;

  Multiplexer #(.width(4)) multiplexer_1 (.in0(4'b0011), .in1(4'b0010), .out(multiplexer_1_out), .sel(IsRType));
  Register #(.width(4)) register_1 (.D(multiplexer_6_out), .clk(CLK), .Q(CurrentState), .clr(RESET));  // open: en
  Multiplexer #(.width(4)) multiplexer_2 (
    .in0(multiplexer_1_out), .in1(4'b0100), .out(multiplexer_2_out), .sel(or_1_out));
  or or_1 (or_1_out, IsLoad, IsStore);
  Multiplexer #(.width(4)) multiplexer_3 (.in0(4'b0000), .in1(4'b1101), .out(V0Mux), .sel(V0));
  Comparator #(.width(32)) comparator_1 (.a(V0_Val), .b(32'ha), .eq(V0));  // open: gt, lt
  Multiplexer #(.width(4)) multiplexer_4 (
    .in0(multiplexer_2_out), .in1(4'b1010), .out(multiplexer_4_out), .sel(IsBranch));
  Multiplexer #(.width(4)) multiplexer_5 (
    .in0(multiplexer_4_out), .in1(4'b1011), .out(multiplexer_5_out), .sel(IsJump));
  Multiplexer #(.select(4), .width(4)) multiplexer_6 (
    .in0(4'b0001), .in1(S_ID), .in2(4'b0111), .in3(4'b1000), .in4(IsLoadMux), .in5(4'b1001), .in6(4'b0000),
    .in7(4'b0000), .in8(4'b0000), .in9(4'b0000), .in10(4'b0000), .in11(4'b0000), .in12(V0Mux),
    .in13(4'b0000), .in14(4'b0000), .in15(4'b0000), .out(multiplexer_6_out), .sel(CurrentState));
  Multiplexer #(.width(4)) multiplexer_7 (.in0(4'b0110), .in1(4'b0101), .out(IsLoadMux), .sel(IsLoad));
  Multiplexer #(.width(4)) multiplexer_8 (.in0(multiplexer_5_out), .in1(4'b0000), .out(multiplexer_8_out), .sel(IsJr));
  Decoder #(.select(4)) decoder_1 (
    .out0(IRWrite), .out1(decoder_1_out1), .out2(decoder_1_out2), .out3(decoder_1_out3),
    .out4(decoder_1_out4), .out5(decoder_1_out5), .out6(MEM_WE), .out7(RegDst[0]), .out8(decoder_1_out8),
    .out9(MemToReg[0]), .out10(PCWriteCond), .out11(decoder_1_out11), .out12(decoder_1_out12),
    .out13(decoder_1_out13), .sel(CurrentState));  // open: out14, out15, en
  Multiplexer #(.width(4)) multiplexer_9 (
    .in0(multiplexer_8_out), .in1(4'b1100), .out(multiplexer_9_out), .sel(IsSyscall));
  Multiplexer #(.width(4)) multiplexer_10 (.in0(multiplexer_9_out), .in1(4'b1101), .out(S_ID), .sel(Illegal));
  and and_1 (and_1_out, IsJr, decoder_1_out1);
  or or_2 (PCWrite, IRWrite, decoder_1_out11, and_1_out);
  or or_3 (ALUSrcA, decoder_1_out2, decoder_1_out3, decoder_1_out4, PCWriteCond);
  or or_4 (ALUSrcB[1], decoder_1_out11, decoder_1_out2, decoder_1_out3);
  and and_2 (TTY_WE, decoder_1_out12, V0);
  or or_5 (PCSource[0], decoder_1_out1, PCWriteCond);
  or or_6 (PCSource[1], decoder_1_out1, decoder_1_out11);
  or or_7 (IorD, decoder_1_out5, MEM_WE);
  and and_3 (MemToReg[1], decoder_1_out11, IsJal);
  or or_8 (ALUSrcB[0], IRWrite, decoder_1_out1);
  or or_9 (HALT, decoder_1_out13, Illegal);
  or or_10 (RegWrite, RegDst[0], decoder_1_out8, MemToReg[0]);

  assign RegDst[1] = MemToReg[1];

  // Other names for the same wires on the sheet: V[31:0] = V0_Val

  // Notes on the sheet:
  //   S_EX_I
  //   S_EX_R
  //   S_EX_M
  //   S_IF
  //   S_EX_R
  //   S_EX_I
  //   S_MEM_R
  //   S6 = S_MEM_W (6)
  //   S7 = S_WB_R (7)
  //   S8 = S_WB_I (8)
  //   S9 = S_WB_LD (9)
  //   S10 = S_BR (10)
  //   S11 = S_JUMP (11)
  //   S12 = S_SYS (12)
  //   S13 = S_HALT (13)
  //   S_BR
  //   S_MEM_W
  //   S_MEM_R
  //   S_JUMP
  //   S_IF
  //   S_SYS
  //   S_HALT
endmodule

module Branch_Control (
  input  PCWrite,
  input  PCWriteCond,
  input  IsBeq,
  input  IsBne,
  input  Zero,
  output PCWriteFinal
);

  wire and_1_out, and_2_out, and_3_out, not_1_out, or_1_out;

  not not_1 (not_1_out, Zero);
  and and_1 (and_1_out, IsBeq, Zero);
  and and_2 (and_2_out, not_1_out, IsBne);
  or or_1 (or_1_out, and_1_out, and_2_out);
  and and_3 (and_3_out, PCWriteCond, or_1_out);
  or or_2 (PCWriteFinal, PCWrite, and_3_out);

  // Notes on the sheet:
  //   PCWrite | 1 bit (Viene de la FSM: 1 indica que hay que escribir el PC obligatoriamente)
  //   PCWriteCond | 1 bit (Viene de la FSM: 1 indica que estamos evaluando un branch)
  //   IsBeq | 1 bit (Viene del Decoder: 1 si es beq)
  //   IsBne | 1 bit (Viene del Decoder: 1 si es bne)
  //   Zero | 1 bit (Viene de la ALU: 1 si la resta de $rs - $rt dio 0)
  //   Lógica BEQ: BeqTaken = IsBeq AND Zero 
  //   Lógica BNE: BneTaken = IsBne AND (NOT Zero) 
  //   Branch Tomado: BranchTaken = BeqTaken OR BneTaken
  //   Condición de Salto: BranchWrite = PCWriteCond AND BranchTaken 
  //   Decisión Final: PCWriteFinal=PCWrite OR BranchWrite
  //   BeqTaken
  //   BneTaken
  //   BranchTaken
  //   BranchWrite
  //   PCWriteFinal | 1 bit (Va directamente a la habilitación de carga Enable del registro PC en el Datapath)
endmodule
